# Fritzing sketch BotAstra_ (saved by Fritzing 0.9.3b)
breadboards: 4

parts:
  RCWL1 = IC, SIP package, 5 pins [chip_label=RCWL-0516]
  Part1 = Arduino Mega 2560 (Rev3)
  LED1 = LED - 5mm [color="Red (633nm)" package="5 mm [THT]"]
  LED2 = LED - 5mm [color="Yellow (595nm)" package="5 mm [THT]"]
  LED3 = LED - 5mm [color="Green (555nm)" package="5 mm [THT]"]
  R1 = Resistor [tolerance=±5% resistance=220 package=THT]
  R2 = Resistor [tolerance=±5% resistance=220 package=THT]
  R3 = Resistor [tolerance=±5% resistance=220 package=THT]
  LED4 = LED - 5mm [color="Red (633nm)" package="5 mm [THT]"]
  LED5 = LED - 5mm [color="Yellow (595nm)" package="5 mm [THT]"]
  LED6 = LED - 5mm [color="Green (555nm)" package="5 mm [THT]"]
  R4 = Resistor [tolerance=±5% resistance=220 package=THT]
  R5 = Resistor [tolerance=±5% resistance=220 package=THT]
  R6 = Resistor [tolerance=±5% resistance=220 package=THT]
  RCWL2 = IC, SIP package, 5 pins [chip_label=RCWL-0516]  # not connected
  LED7 = LED - 5mm [color="Red (633nm)" package="5 mm [THT]"]
  LED8 = LED - 5mm [color="Yellow (595nm)" package="5 mm [THT]"]
  LED9 = LED - 5mm [color="Green (555nm)" package="5 mm [THT]"]
  R7 = Resistor [tolerance=±5% resistance=220 package=THT]
  R8 = Resistor [tolerance=±5% resistance=220 package=THT]
  R9 = Resistor [tolerance=±5% resistance=220 package=THT]
  RCWL3 = IC, SIP package, 5 pins [chip_label=RCWL-0516]
  LED10 = LED - 5mm [color="Red (633nm)" package="5 mm [THT]"]
  LED11 = LED - 5mm [color="Yellow (595nm)" package="5 mm [THT]"]
  LED12 = LED - 5mm [color="Green (555nm)" package="5 mm [THT]"]
  R10 = Resistor [tolerance=±5% resistance=220 package=THT]
  R11 = Resistor [tolerance=±5% resistance=220 package=THT]
  R12 = Resistor [tolerance=±5% resistance=220 package=THT]
  RCWL4 = IC, SIP package, 5 pins [chip_label=RCWL-0516]  # not connected
  RCWL5 = IC, SIP package, 5 pins [chip_label=RCWL-0516]  # not connected

nets:
  N1: RCWL1.pin2, Part1.GND, R1.Pin_0, R2.Pin_0, R3.Pin_1, R4.Pin_0, R5.Pin_0, R6.Pin_1, R7.Pin_0, R8.Pin_0, R9.Pin_1, R10.Pin_0, R11.Pin_0, R12.Pin_1
  N2: RCWL1.pin3, Part1.D53
  N3: RCWL1.pin4, Part1.5V, RCWL3.pin4
  N4: Part1.D13_PWM, LED4.anode
  N5: Part1.D12_PWM, LED5.anode
  N6: Part1.D11_PWM, LED6.cathode, R5.Pin_1
  N7: Part1.D10_PWM, LED7.anode
  N8: Part1.D9_PWM, LED8.anode
  N9: Part1.D8_PWM, LED9.anode
  N10: Part1.D23, LED1.anode
  N11: Part1.D25, LED2.anode
  N12: Part1.D27, LED3.anode
  N13: Part1.D44, LED10.anode
  N14: Part1.D46, LED11.anode
  N15: Part1.D48, LED12.anode
  N16: Part1.D52, RCWL3.pin3
  N17: LED1.cathode, R1.Pin_1
  N18: LED3.cathode, R2.Pin_1
  N19: LED4.cathode, R4.Pin_1
  N20: LED7.cathode, R7.Pin_1
  N21: LED9.cathode, R8.Pin_1
  N22: LED10.cathode, R10.Pin_1
  N23: LED12.cathode, R11.Pin_1
